# Fritzing sketch circuit_layout (saved by Fritzing 0.8.7b)
breadboards: 1

parts:
  元件1 = Arduino Uno (Rev3)
  LED1 = LED - 5mm [color="Red (633nm)" package="5 mm [THT]"]
  LED2 = LED - 5mm [color="Red (633nm)" package="5 mm [THT]"]
  LED3 = LED - 5mm [color="Red (633nm)" package="5 mm [THT]"]
  R1 = Resistor [tolerance=±5% resistance=220 package=THT]
  R2 = Resistor [tolerance=±5% resistance=220 package=THT]
  R3 = Resistor [tolerance=±5% resistance=220 package=THT]
  LED4 = LED - 5mm [color="Red (633nm)" package="5 mm [THT]"]
  LED5 = LED - 5mm [color="Red (633nm)" package="5 mm [THT]"]
  LED6 = LED - 5mm [color="Red (633nm)" package="5 mm [THT]"]
  LED7 = LED - 5mm [color="Red (633nm)" package="5 mm [THT]"]
  LED8 = LED - 5mm [color="Red (633nm)" package="5 mm [THT]"]
  R4 = Resistor [tolerance=±5% resistance=220 package=THT]
  R5 = Resistor [tolerance=±5% resistance=220 package=THT]
  R6 = Resistor [tolerance=±5% resistance=220 package=THT]
  R7 = Resistor [tolerance=±5% resistance=220 package=THT]
  R8 = Resistor [tolerance=±5% resistance=220 package=THT]
  U1 = 74HC595 [package="DIP16 [THT]"]

nets:
  N1: 元件1.D8, U1.ST_CP
  N2: 元件1.D11_PWM/MOSI, U1.DS
  N3: 元件1.D12/MISO, U1.SH_CP
  3V3: 元件1.3V3, U1.MR, U1.VCC
  GND: 元件1.GND, R1.Pin_1, R2.Pin_1, R3.Pin_1, R4.Pin_1, R5.Pin_1, R6.Pin_1, R7.Pin_1, R8.Pin_1, U1.GND, U1.OE
  N4: LED1.cathode, R1.Pin_0
  N5: LED1.anode, U1.Q7
  N6: LED2.cathode, R2.Pin_0
  N7: LED2.anode, U1.Q6
  N8: LED3.cathode, R3.Pin_0
  N9: LED3.anode, U1.Q5
  N10: LED4.cathode, R5.Pin_0
  N11: LED4.anode, U1.Q3
  N12: LED5.cathode, R6.Pin_0
  N13: LED5.anode, U1.Q2
  N14: LED6.cathode, R7.Pin_0
  N15: LED6.anode, U1.Q1
  N16: LED7.cathode, R4.Pin_0
  N17: LED7.anode, U1.Q4
  N18: LED8.cathode, R8.Pin_0
  N19: LED8.anode, U1.Q0
